# Fritzing sketch Neopixel_esp8266 (saved by Fritzing 0.9.2b)

parts:
  JACK1 = 2.1mm Barrel Jack with Terminal Block
  neopixel1 = Neopixel Ring 16
  C1 = Electrolytic Capacitor [capacitance=1mF voltage=16V package="0807 [SMD, electrolytic]"]
  U1 = NodeMCU V1.0

nets:
  VCC: JACK1.POS, neopixel1.VCC, C1.+, U1.Vin
  GND: JACK1.NEG, neopixel1.GND, C1.-, U1.GND
  N1: neopixel1.IN, U1.D4

custom parts:
  Neopixel Ring 16: Neopixel Ring x16
  NodeMCU V1.0: ESP8266 based NodeMCU
